# Fritzing sketch sketch_rpi (saved by Fritzing 0.9.3b)
circuit board: 6.74804cm x 6.13649cm

parts:
  Raspberry_Pi_Zero1 = Raspberry Pi Zero
  U1 = ENCODER-QUADRATURE [package=encoder-16mm-quad]
  S1 = Pushbutton [package=THT]
  OLED1 = OLED 128x64 I2C Monochrome Display

nets:
  3V3: Raspberry_Pi_Zero1.3v3, OLED1.VDD
  N1: Raspberry_Pi_Zero1.GPIO2, OLED1.SDA
  N2: Raspberry_Pi_Zero1.GPIO3, OLED1.SCK
  GND: Raspberry_Pi_Zero1.GND, U1.C, S1.leg0, OLED1.GND
  N3: Raspberry_Pi_Zero1.GIPO18, S1.leg1
  N4: Raspberry_Pi_Zero1.GIPO15, U1.A
  N5: Raspberry_Pi_Zero1.GIPO14, U1.B
